// Digital circuit Capstone.dig as structural Verilog
module Capstone (
  input  [1:0] C,
  input  rst,
  input  clk
);

  wire and_1_out, and_2_out, and_3_out, and_4_out, and_5_out, and_6_out, and_7_out, and_8_out, and_9_out,
       and_10_out, and_11_out, and_12_out, and_13_out, and_14_out, and_15_out, and_16_out, and_17_out,
       and_18_out, and_19_out, and_20_out, C_0_t, C_1_t, or_1_out, or_2_out, or_3_out, or_4_out, Q_0, Q_0_t,
       Q_1, Q_1_t, Q_2, Q_2_t, Q_3, Q_3_t, x_0, x_1, x_3;

  and and_1 (and_1_out, Q_3_t, Q_0, C[1], C[0]);
  and and_2 (and_2_out, Q_3_t, Q_1, C[1], C[0]);
  and and_3 (and_3_out, Q_3, Q_1_t, Q_0_t, C[1], C[0]);
  and and_4 (and_4_out, Q_3_t, Q_0, C_1_t, C_0_t);
  and and_5 (and_5_out, Q_3_t, Q_1, C_1_t, C_0_t);
  and and_6 (and_6_out, Q_3, C_1_t, C_0_t);
  and and_7 (and_7_out, Q_3, Q_2_t, Q_0, C[1], C_0_t);
  and and_8 (and_8_out, Q_3, Q_2, Q_0_t, C_0_t);
  or or_1 (or_1_out, and_1_out, and_2_out, and_3_out);
  or or_2 (or_2_out, and_4_out, and_5_out, and_6_out, and_7_out, and_8_out);
  and and_9 (and_9_out, Q_3_t, Q_1, C[1]);
  and and_10 (and_10_out, Q_3_t, Q_0, C[1]);
  and and_11 (and_11_out, Q_3, Q_1_t, Q_0_t, C[1]);
  and and_12 (and_12_out, Q_2_t, Q_0, C[1], C_0_t);
  and and_13 (and_13_out, Q_0, C_1_t, C[0]);
  and and_14 (and_14_out, Q_1, C_1_t, C[0]);
  and and_15 (and_15_out, Q_3, Q_1_t, Q_0_t, C[0]);
  and and_16 (and_16_out, Q_3, Q_2_t, Q_1_t, Q_0_t, C[1]);
  or or_3 (or_3_out, and_9_out, and_10_out, and_11_out, and_12_out);
  or or_4 (or_4_out, and_13_out, and_14_out, and_15_out, and_16_out);
  D_FF_AS d_ff_as_1 (.Set(1'b0), .D(or_3_out), .C(clk), .Clr(rst), .Q(Q_3), .nQ(Q_3_t));
  D_FF_AS d_ff_as_2 (.Set(1'b0), .D(or_1_out), .C(clk), .Clr(rst), .Q(Q_2), .nQ(Q_2_t));
  D_FF_AS d_ff_as_3 (.Set(1'b0), .D(or_2_out), .C(clk), .Clr(rst), .Q(Q_1), .nQ(Q_1_t));
  D_FF_AS d_ff_as_4 (.Set(rst), .D(or_4_out), .C(clk), .Clr(1'b0), .Q(Q_0), .nQ(Q_0_t));
  not not_1 (C_0_t, C[0]);
  not not_2 (C_1_t, C[1]);
  Seven_Seg_Hex seven_seg_hex_1 (.d({x_3, Q_2_t, x_1, x_0}), .dp(1'b0));
  or or_5 (x_3, Q_1_t, Q_3);
  and and_17 (and_17_out, Q_1_t, Q_0_t);
  and and_18 (and_18_out, Q_3, Q_2_t);
  and and_19 (and_19_out, Q_2_t, Q_1);
  and and_20 (and_20_out, Q_2_t, Q_0);
  or or_6 (x_1, and_17_out, Q_3);
  or or_7 (x_0, and_18_out, and_19_out, and_20_out);

  // Other names for the same wires on the sheet: C_0 = C[0]; C_1 = C[1]; x_2 = Q_2_t
endmodule
