// Digital circuit addr_gen.dig as structural Verilog
module addr_gen (
  input  zero,
  input  [3:0] data__bus,
  input  clk,
  input  reset,
  input  use__pc,
  input  load__mar,
  input  jump,
  input  brz,
  output [3:0] addr__bus
);

  wire and_1_out, not_1_out, or_1_out;
  wire [3:0] mar, pc;

  and and_1 (and_1_out, brz, zero);
  or or_1 (or_1_out, jump, and_1_out);
  program_ctr program_ctr_1 (
    .enable(use__pc), .reset(reset), .clk(clk), .load__pc(or_1_out), .data__bus(data__bus), .q(pc));
  four_bit_reg four_bit_reg_1 (.d(data__bus), .enable(load__mar), .reset(reset), .clk(clk), .q(mar));
  not not_1 (not_1_out, use__pc);
  four_bit_mux four_bit_mux_1 (.a(pc), .b(mar), .sel(not_1_out), .y(addr__bus));
endmodule
