// Digital circuit brainless.dig as structural Verilog
module brainless (
  input  [3:0] addr__bus,
  input  [3:0] data__in,
  input  arith,
  input  invert,
  input  pass,
  input  load__acc,
  input  acc__to__db,
  input  read,
  input  write,
  input  clk,
  input  reset,
  output [3:0] alu__out,
  output [3:0] accum,
  output [3:0] data__bus,
  output zero
);

  wire [3:0] four_bit_mux_2_y, program_ram_1_data__out;

  alu alu_1 (
    .a(data__bus), .b(accum), .invert(invert), .arith(arith), .pass(pass), .cin(1'b0), .y(alu__out));  // open: cout, overfl
  and and_1 (zero, ~accum[0], ~accum[1], ~accum[2], ~accum[3]);  // And
  four_bit_reg four_bit_reg_1 (.d(alu__out), .enable(load__acc), .reset(reset), .clk(clk), .q(accum));
  four_bit_mux four_bit_mux_1 (.a(four_bit_mux_2_y), .b(accum), .sel(acc__to__db), .y(data__bus));
  program_ram program_ram_1 (
    .data__in(data__bus), .addr(addr__bus), .clk(clk), .write(write), .data__out(program_ram_1_data__out));
  four_bit_mux four_bit_mux_2 (.a(data__in), .b(program_ram_1_data__out), .sel(read), .y(four_bit_mux_2_y));
endmodule
