// Digital circuit controller.dig as structural Verilog
module controller (
  input  load__ir,
  input  [3:0] data__bus,
  input  reset,
  input  clk,
  output [11:0] control,
  output [3:0] instr__reg
);

  wire [1:0] step__reg;
  wire [13:12] rom__out;

  four_bit_reg four_bit_reg_1 (.d(data__bus), .enable(load__ir), .reset(reset), .clk(clk), .q(instr__reg));
  two_bit_reg two_bit_reg_1 (.d(rom__out), .enable(1'b1), .reset(reset), .clk(clk), .q(step__reg));
  ROM #(.AddrBits(6), .Bits(14)) microcode_ROM (.A({instr__reg, step__reg}), .sel(1'b1), .D({rom__out, control}));

  // Other names for the same wires on the sheet: rom__out[11:0] = control

  // Notes on the sheet:
  //   Instruction Reg
  //   Step Reg
  //   contents of microcode_ROM (hex, n*v repeats v):
  //   1205,234,0,0,1205,294,0,0,1205,1000,0,0,1205,214,0,0,1205,d8,0,0
  //   ,1205,2d4,0,0,1205,2304,10a,0,1205,30,0,0,1205,604,0,0,1205,a04,fff
endmodule
