// Digital circuit microprocessor_old.dig as structural Verilog
module microprocessor_old (
  input  clk,
  input  reset,
  input  [3:0] data__in,
  output [3:0] accum,
  output [3:0] addr__bus,
  output [3:0] data__bus,
  output [3:0] instr__reg
);

  wire brainless_1_zero;
  wire [11:0] controller_1_control;

  addr_gen addr_gen_1 (
    .zero(brainless_1_zero), .data__bus(data__bus), .clk(clk), .reset(reset),
    .use__pc(controller_1_control[9]), .load__mar(controller_1_control[8]), .jump(controller_1_control[10]),
    .brz(controller_1_control[11]), .addr__bus(addr__bus));
  controller controller_1 (
    .load__ir(controller_1_control[0]), .data__bus(data__bus), .reset(reset), .clk(clk),
    .control(controller_1_control), .instr__reg(instr__reg));
  brainless brainless_1 (
    .addr__bus(addr__bus), .data__in(data__in), .arith(controller_1_control[7]),
    .invert(controller_1_control[6]), .pass(controller_1_control[5]), .load__acc(controller_1_control[4]),
    .acc__to__db(controller_1_control[3]), .read(controller_1_control[2]), .write(controller_1_control[1]),
    .clk(clk), .reset(reset), .accum(accum), .data__bus(data__bus), .zero(brainless_1_zero));  // open: alu__out

  // Notes on the sheet:
  //   clk: pin B8
  //   reset: pin A7
  //   data__in: pin C10, C11, D12, C12
  //   accum: pin J20, K20, L18, N18, M20, N19, N20
  //   addr__bus: pin C18, D18, E18, B16, A17, A18, B17
  //   data__bus: pin C14, E15, C15, C16, E16, D17, C17
  //   instr__reg: pin B20, A20, B19, A21, B21, C22, B22
endmodule
