// Digital circuit program_ctr.dig as structural Verilog
module program_ctr (
  input  enable,
  input  reset,
  input  clk,
  input  load__pc,
  input  [3:0] data__bus,
  output [3:0] q
);

  wire [3:0] four_bit_mux_1_y, incrementer_1_y;

  four_bit_mux four_bit_mux_1 (.a(q), .b(data__bus), .sel(load__pc), .y(four_bit_mux_1_y));
  incrementer incrementer_1 (.inc(1'b1), .a(four_bit_mux_1_y), .y(incrementer_1_y));  // open: cry
  four_bit_reg four_bit_reg_1 (.d(incrementer_1_y), .enable(enable), .reset(reset), .clk(clk), .q(q));
endmodule
