// Digital circuit segments.dig as structural Verilog
module segments (
  input  [3:0] hex__in,
  output [6:0] segs__out
);

  LookUpTable #(.Bits(7)) segmenter (
    .in0(hex__in[0]), .in1(hex__in[1]), .in2(hex__in[2]), .in3(hex__in[3]), .out(segs__out));

  // Notes on the sheet:
  //   contents of segmenter (hex, n*v repeats v):
  //   40,79,24,30,19,12,2,78,0,10,8,3,46,21,6,e
endmodule
