// Digital circuit incrementer.dig as structural Verilog
module incrementer (
  input  inc,
  input  [3:0] a,
  output [3:0] y,
  output cry
);

  wire half_adder_2_cry, half_adder_3_cry, half_adder_4_cry;

  half_adder half_adder_1 (.a(half_adder_2_cry), .b(a[3]), .sum(y[3]), .cry(cry));
  half_adder half_adder_2 (.a(half_adder_3_cry), .b(a[2]), .sum(y[2]), .cry(half_adder_2_cry));
  half_adder half_adder_3 (.a(half_adder_4_cry), .b(a[1]), .sum(y[1]), .cry(half_adder_3_cry));
  half_adder half_adder_4 (.a(a[0]), .b(inc), .sum(y[0]), .cry(half_adder_4_cry));
endmodule
