// Digital circuit alu.dig as structural Verilog
module alu (
  input  [3:0] a,
  input  invert,
  input  [3:0] b,
  input  arith,
  input  cin,
  input  pass,
  output cout,
  output overfl,
  output [3:0] y
);

  wire [3:0] not_neg_1_y;

  not_neg not_neg_1 (.a(a), .invert(invert), .neg(arith), .y(not_neg_1_y));  // open: cry
  and_add and_add_1 (.a(not_neg_1_y), .b(b), .cin(cin), .add(arith), .pass(pass), .cout(cout), .overfl(overfl), .y(y));
endmodule
