// Digital circuit microprocessor.dig as structural Verilog
module microprocessor (
  input  clk,
  input  reset,
  input  [3:0] data__in,
  output [3:0] accum
);

  wire [3:0] addr_gen_1_addr__bus, brainless_1_data__bus;
  wire [9:0] controller_1_control;

  addr_gen addr_gen_1 (
    .data__bus(brainless_1_data__bus), .use__pc(controller_1_control[9]),
    .load__mar(controller_1_control[8]), .clk(clk), .reset(reset), .addr__bus(addr_gen_1_addr__bus));
  controller controller_1 (
    .load__ir(controller_1_control[0]), .data__bus(brainless_1_data__bus), .reset(reset), .clk(clk),
    .control(controller_1_control));
  brainless brainless_1 (
    .addr__bus(addr_gen_1_addr__bus), .data__in(data__in), .arith(controller_1_control[7]),
    .invert(controller_1_control[6]), .pass(controller_1_control[5]), .load__acc(controller_1_control[4]),
    .acc__to__db(controller_1_control[3]), .read(controller_1_control[2]), .write(controller_1_control[1]),
    .clk(clk), .reset(reset), .accum(accum), .data__bus(brainless_1_data__bus));  // open: alu__out
endmodule
